// Logisim project lcd2.circ as structural Verilog: 1 circuit, main circuit main
module main (
  input  [7:0] in_1,
  input  [7:0] in_2,
  input  [7:0] in_3,
  input  in_4,
  output out_5,
  output out_6
);

  wire clock_1_out, dip_74139_1_p4, dip_74139_1_p5, dip_74139_1_p6, dip_74139_1_p7;
  wire [7:0] multiplexer_1_out, multiplexer_2_out, multiplexer_3_out, multiplexer_4_out, rom_1_data,
       rom_2_data;

  Clock clock_1 (.out(clock_1_out));
  // DIP_7476 dip_7476_1: pin names not known; wires that end beside it: clock_1_out, 1'b1, out_6, 1'b1, out_6, 1'b1, out_5, 1'b1
  // DIP_74139 dip_74139_1: pin names not known; wires that end beside it: 1'b0, out_6, out_5, dip_74139_1_p4, dip_74139_1_p5, dip_74139_1_p6, dip_74139_1_p7
  // Probe on in_3
  // Probe on in_3
  ROM rom_1 (.addr(in_1), .data(rom_1_data), .sel(1'b1));
  _7_Segment_Display u_7_segment_display_1 (
    .g(rom_1_data[0]), .f(rom_1_data[1]), .a(rom_1_data[6]), .b(rom_1_data[5]), .e(rom_1_data[2]),
    .d(rom_1_data[3]), .c(rom_1_data[4]), .dp(rom_1_data[7]));
  ROM #(.addrWidth(11)) rom_2 (.addr({in_4, out_5, out_6, in_3}), .data(rom_2_data));  // open: sel
  Multiplexer #(.width(8), .enable("false")) multiplexer_1 (
    .in0(rom_2_data), .in1({8{1'b0}}), .out(multiplexer_1_out), .sel(dip_74139_1_p7));
  Multiplexer #(.width(8), .enable("false")) multiplexer_2 (
    .in0(rom_2_data), .in1({8{1'b0}}), .out(multiplexer_2_out), .sel(dip_74139_1_p6));
  Multiplexer #(.width(8), .enable("false")) multiplexer_3 (
    .in0(rom_2_data), .in1({8{1'b0}}), .out(multiplexer_3_out), .sel(dip_74139_1_p5));
  Multiplexer #(.width(8), .enable("false")) multiplexer_4 (
    .in0(rom_2_data), .in1({8{1'b0}}), .out(multiplexer_4_out), .sel(dip_74139_1_p4));
  _7_Segment_Display u_7_segment_display_2 (
    .g(multiplexer_1_out[0]), .f(multiplexer_1_out[1]), .a(multiplexer_1_out[6]), .b(multiplexer_1_out[5]),
    .e(multiplexer_1_out[2]), .d(multiplexer_1_out[3]), .c(multiplexer_1_out[4]), .dp(multiplexer_1_out[7]));
  _7_Segment_Display u_7_segment_display_3 (
    .g(in_2[0]), .f(in_2[1]), .a(in_2[6]), .b(in_2[5]), .e(in_2[2]), .d(in_2[3]), .c(in_2[4]), .dp(in_2[7]));
  _7_Segment_Display u_7_segment_display_4 (
    .g(multiplexer_3_out[0]), .f(multiplexer_3_out[1]), .a(multiplexer_3_out[6]), .b(multiplexer_3_out[5]),
    .e(multiplexer_3_out[2]), .d(multiplexer_3_out[3]), .c(multiplexer_3_out[4]), .dp(multiplexer_3_out[7]));
  _7_Segment_Display u_7_segment_display_5 (
    .g(multiplexer_2_out[0]), .f(multiplexer_2_out[1]), .a(multiplexer_2_out[6]), .b(multiplexer_2_out[5]),
    .e(multiplexer_2_out[2]), .d(multiplexer_2_out[3]), .c(multiplexer_2_out[4]), .dp(multiplexer_2_out[7]));
  _7_Segment_Display u_7_segment_display_6 (
    .g(multiplexer_4_out[0]), .f(multiplexer_4_out[1]), .a(multiplexer_4_out[6]), .b(multiplexer_4_out[5]),
    .e(multiplexer_4_out[2]), .d(multiplexer_4_out[3]), .c(multiplexer_4_out[4]), .dp(multiplexer_4_out[7]));

  // Notes on the sheet:
  //   contents of rom_1 (hex, n*v repeats v):
  //   7e 30 6d 79 33 5b 5f 70 7f 7b
  //   contents of rom_2 (hex, n*v repeats v):
  //   7e 30 6d 79 33 5b 5f 70 7f 7b 7e 30 6d 79 33 5b 5f 70 7f 7b 7e 30 6d 79 33 5b 5f 70 7f 7b 7e 30 6d
  //   79 33 5b 5f 70 7f 7b 7e 30 6d 79 33 5b 5f 70 7f 7b 7e 30 6d 79 33 5b 5f 70 7f 7b 7e 30 6d 79 33 5b
  //   5f 70 7f 7b 7e 30 6d 79 33 5b 5f 70 7f 7b 7e 30 6d 79 33 5b 5f 70 7f 7b 7e 30 6d 79 33 5b 5f 70 7f
  //   7b 7e 30 6d 79 33 5b 5f 70 7f 7b 7e 30 6d 79 33 5b 5f 70 7f 7b 7e 30 6d 79 33 5b 5f 70 7f 7b 7e 30
  //   6d 79 33 5b 5f 70 7f 7b 7e 30 6d 79 33 5b 5f 70 7f 7b 7e 30 6d 79 33 5b 5f 70 7f 7b 7e 30 6d 79 33
  //   5b 5f 70 7f 7b 7e 30 6d 79 33 5b 5f 70 7f 7b 7e 30 6d 79 33 5b 5f 70 7f 7b 7e 30 6d 79 33 5b 5f 70
  //   7f 7b 7e 30 6d 79 33 5b 5f 70 7f 7b 7e 30 6d 79 33 5b 5f 70 7f 7b 7e 30 6d 79 33 5b 5f 70 7f 7b 7e
  //   30 6d 79 33 5b 5f 70 7f 7b 7e 30 6d 79 33 5b 5f 70 7f 7b 7e 30 6d 79 33 5b 10*7e 10*30 10*6d 10*79
  //   10*33 10*5b 10*5f 10*70 10*7f 10*7b 10*7e 10*30 10*6d 10*79 10*33 10*5b 10*5f 10*70 10*7f 10*7b
  //   10*7e 10*30 10*6d 10*79 10*33 6*5b 100*7e 100*30 56*6d 256*0 7e 30 6d 79 33 5b 5f 70 7f 7b 7e 30 6d
  //   79 33 5b 5f 70 7f 7b 7e 30 6d 79 33 5b 5f 70 7f 7b 7e 30 6d 79 33 5b 5f 70 7f 7b 7e 30 6d 79 33 5b
  //   5f 70 7f 7b 7e 30 6d 79 33 5b 5f 70 7f 7b 7e 30 6d 79 33 5b 5f 70 7f 7b 7e 30 6d 79 33 5b 5f 70 7f
  //   7b 7e 30 6d 79 33 5b 5f 70 7f 7b 7e 30 6d 79 33 5b 5f 70 7f 7b 7e 30 6d 79 33 5b 5f 70 7f 7b 7e 30
  //   6d 79 33 5b 5f 70 7f 7b 7e 30 6d 79 33 5b 5f 70 7f 70 5f 5b 33 79 6d 30 7e 7b 7f 70 5f 5b 33 79 6d
  //   30 7e 7b 7f 70 5f 5b 33 79 6d 30 7e 7b 7f 70 5f 5b 33 79 6d 30 7e 7b 7f 70 5f 5b 33 79 6d 30 7e 7b
  //   7f 70 5f 5b 33 79 6d 30 7e 7b 7f 70 5f 5b 33 79 6d 30 7e 7b 7f 70 5f 5b 33 79 6d 30 7e 7b 7f 70 5f
  //   5b 33 79 6d 30 7e 7b 7f 70 5f 5b 33 79 6d 30 7e 7b 7f 70 5f 5b 33 79 6d 30 7e 7b 7f 70 5f 5b 33 79
  //   6d 30 7e 7b 7f 70 5f 5b 33 79 6d 30 10*7e 10*30 10*6d 10*79 10*33 10*5b 10*5f 10*70 10*7f 10*7b
  //   10*7e 10*30 17*6d 10*30 10*7e 10*7b 10*7f 10*70 10*5f 10*5b 10*33 10*79 10*6d 10*30 109*7e 57*30
  //   99*7e 128*0 128*1
endmodule
